# Fritzing sketch Breadboard (saved by Fritzing 0.9.3b)
breadboards: 3

parts:
  U1 = atmega328 [package=dip]
  XTAL1 = Crystal [frequency="16 Mhz" package=THT]
  C1 = Ceramic Capacitor [capacitance=22pF package="100 mil [THT, multilayer]"]
  C2 = Ceramic Capacitor [capacitance=22pF package="100 mil [THT, multilayer]"]
  R1 = Resistor [tolerance=±5% resistance=10k package=THT]
  Part1 = Real Time Clock Module - DS1307 RTC Breakout Board
  R2 = Rotary Potentiometer (Large) [maximum_resistance=100kΩ package=THT]
  Q1 = Basic FET N-Channel [package="TO220 [THT]"]
  L1 = Inductor [package="400 mil [THT]"]
  D1 = Rectifier Diode [part_number=1N4001 package="300 mil [THT]"]
  C3 = Electrolytic Capacitor [capacitance=0.47mF voltage=0.1kV package="100 mil [THT, electrolytic]"]
  C4 = Ceramic Capacitor [capacitance=100nF package="100 mil [THT, multilayer]"]
  U2 = 74HC595 [package="DIP16 [THT]"]
  U3 = 74HC595 [package="DIP16 [THT]"]
  U4 = 74HC595 [package="DIP16 [THT]"]
  IC1 = IC, DIP package, 16 pins [chip_label=K155ID1]
  IC2 = IC, DIP package, 16 pins [chip_label=K155ID1]
  IC3 = IC, DIP package, 16 pins [chip_label=K155ID1]
  IC4 = IC, DIP package, 16 pins [chip_label=K155ID1]
  IC5 = IC, DIP package, 16 pins [chip_label=K155ID1]
  IC6 = IC, DIP package, 16 pins [chip_label=K155ID1]
  NIXIE1 = IN-12 Nixie tube [part_number=IN-12B]
  NIXIE2 = IN-12 Nixie tube [part_number=IN-12B]
  NIXIE3 = IN-12 Nixie tube [part_number=IN-12B]
  NIXIE4 = IN-12 Nixie tube [part_number=IN-12B]
  NIXIE5 = IN-12 Nixie tube [part_number=IN-12B]
  NIXIE6 = IN-12 Nixie tube [part_number=IN-12B]
  S1 = Toggle Switch [package=THT]
  R3 = Resistor [tolerance=±5% resistance=1M package=THT]
  X2 = USB Connectors [package=usb-microb]
  R4 = Resistor [tolerance=±5% resistance=1M package=THT]

nets:
  N1: U1.RESET, R1.Pin_1
  N2: U1.D2, U2.DS
  N3: U1.D3_(PWM), U2.ST_CP, U3.ST_CP, U4.ST_CP
  N4: U1.D4, U2.SH_CP, U3.SH_CP, U4.SH_CP
  VCC: U1.VCC, U1.AVCC, U1.AREF, R1.Pin_0, Part1.5V, R2.leg2, L1.pin_0, U2.MR, U2.VCC, U3.MR, U3.VCC, U4.MR, U4.VCC, IC1.pin5, IC2.pin5, IC3.pin5, IC4.pin5, IC5.pin5, IC6.pin5, S1.COM, X2.VBUS
  GND: U1.GND, C1.1, C2.1, Part1.GND, R2.leg1, Q1.source, C3.-, C4.0, U2.GND, U2.OE, U3.GND, U3.OE, U4.GND, U4.OE, IC1.pin12, IC2.pin12, IC3.pin12, IC4.pin12, IC5.pin12, IC6.pin12, R3.Pin_0, X2.GND, R4.Pin_1
  N5: U1.XLAT1, XTAL1.pin_0, C1.0
  N6: U1.XLAT2, XTAL1.pin_1, C2.0
  N7: U1.D5_(PWM), Q1.drain
  N8: U1.D8, R3.Pin_1
  N9: U1.D9_(PWM), S1.L1, R4.Pin_0
  N10: U1.A0, R2.wiper
  N11: U1.A4, Part1.SDA
  N12: U1.A5, Part1.SCL
  N13: Q1.gate, L1.pin_1, D1.anode
  N14: D1.cathode, C3.+, C4.1, NIXIE1.Anode, NIXIE2.Anode, NIXIE3.Anode, NIXIE4.Anode, NIXIE5.Anode, NIXIE6.Anode
  N15: U2.Q1, IC1.pin4
  N16: U2.Q2, IC1.pin6
  N17: U2.Q3, IC1.pin7
  N18: U2.Q4, IC2.pin3
  N19: U2.Q5, IC2.pin4
  N20: U2.Q6, IC2.pin6
  N21: U2.Q7, IC2.pin7
  N22: U2.Q7', U3.DS
  N23: U2.Q0, IC1.pin3
  N24: U3.Q1, IC3.pin4
  N25: U3.Q2, IC3.pin6
  N26: U3.Q3, IC3.pin7
  N27: U3.Q4, IC4.pin3
  N28: U3.Q5, IC4.pin4
  N29: U3.Q6, IC4.pin6
  N30: U3.Q7, IC4.pin7
  N31: U3.Q7', U4.DS
  N32: U3.Q0, IC3.pin3
  N33: U4.Q1, IC5.pin4
  N34: U4.Q2, IC5.pin6
  N35: U4.Q3, IC5.pin7
  N36: U4.Q4, IC6.pin3
  N37: U4.Q5, IC6.pin4
  N38: U4.Q6, IC6.pin6
  N39: U4.Q7, IC6.pin7
  N40: U4.Q0, IC5.pin3
  N41: IC1.pin1, NIXIE1.Cathode_8
  N42: IC1.pin2, NIXIE1.Cathode_9
  N43: IC1.pin8, NIXIE1.Cathode_2
  N44: IC1.pin9, NIXIE1.Cathode_3
  N45: IC1.pin10, NIXIE1.Cathode_7
  N46: IC1.pin11, NIXIE1.Cathode_6
  N47: IC1.pin13, NIXIE1.Cathode_4
  N48: IC1.pin14, NIXIE1.Cathode_5
  N49: IC1.pin15, NIXIE1.Cathode_1
  N50: IC1.pin16, NIXIE1.Cathode_0
  N51: IC2.pin1, NIXIE2.Cathode_8
  N52: IC2.pin2, NIXIE2.Cathode_9
  N53: IC2.pin8, NIXIE2.Cathode_2
  N54: IC2.pin9, NIXIE2.Cathode_3
  N55: IC2.pin10, NIXIE2.Cathode_7
  N56: IC2.pin11, NIXIE2.Cathode_6
  N57: IC2.pin13, NIXIE2.Cathode_4
  N58: IC2.pin14, NIXIE2.Cathode_5
  N59: IC2.pin15, NIXIE2.Cathode_1
  N60: IC2.pin16, NIXIE2.Cathode_0
  N61: IC3.pin1, NIXIE5.Cathode_8
  N62: IC3.pin2, NIXIE5.Cathode_9
  N63: IC3.pin8, NIXIE5.Cathode_2
  N64: IC3.pin9, NIXIE5.Cathode_3
  N65: IC3.pin10, NIXIE5.Cathode_7
  N66: IC3.pin11, NIXIE5.Cathode_6
  N67: IC3.pin13, NIXIE5.Cathode_4
  N68: IC3.pin14, NIXIE5.Cathode_5
  N69: IC3.pin15, NIXIE5.Cathode_1
  N70: IC3.pin16, NIXIE5.Cathode_0
  N71: IC4.pin1, NIXIE3.Cathode_8
  N72: IC4.pin2, NIXIE3.Cathode_9
  N73: IC4.pin8, NIXIE3.Cathode_2
  N74: IC4.pin9, NIXIE3.Cathode_3
  N75: IC4.pin10, NIXIE3.Cathode_7
  N76: IC4.pin11, NIXIE3.Cathode_6
  N77: IC4.pin13, NIXIE3.Cathode_4
  N78: IC4.pin14, NIXIE3.Cathode_5
  N79: IC4.pin15, NIXIE3.Cathode_1
  N80: IC4.pin16, NIXIE3.Cathode_0
  N81: IC5.pin1, NIXIE6.Cathode_8
  N82: IC5.pin2, NIXIE6.Cathode_9
  N83: IC5.pin8, NIXIE6.Cathode_2
  N84: IC5.pin9, NIXIE6.Cathode_3
  N85: IC5.pin10, NIXIE6.Cathode_7
  N86: IC5.pin11, NIXIE6.Cathode_6
  N87: IC5.pin13, NIXIE6.Cathode_4
  N88: IC5.pin14, NIXIE6.Cathode_5
  N89: IC5.pin15, NIXIE6.Cathode_1
  N90: IC5.pin16, NIXIE6.Cathode_0
  N91: IC6.pin1, NIXIE4.Cathode_8
  N92: IC6.pin2, NIXIE4.Cathode_9
  N93: IC6.pin8, NIXIE4.Cathode_2
  N94: IC6.pin9, NIXIE4.Cathode_3
  N95: IC6.pin10, NIXIE4.Cathode_7
  N96: IC6.pin11, NIXIE4.Cathode_6
  N97: IC6.pin13, NIXIE4.Cathode_4
  N98: IC6.pin14, NIXIE4.Cathode_5
  N99: IC6.pin15, NIXIE4.Cathode_1
  N100: IC6.pin16, NIXIE4.Cathode_0

notes:
  170VDC

custom parts:
  IN-12 Nixie tube: Russian IN-12 Nixie neon indicator tube
